// Logisim project 3-bit Adder.circ as structural Verilog: 1 circuit, main circuit Full adder
module Full_adder (
  input  Cin,
  input  X,
  input  Y,
  input  X2,
  input  Y2,
  input  X3,
  input  Y3,
  output Sum1,
  output Sum2,
  output Sum3,
  output Cout
);

  wire and_1_out, and_2_out, and_3_out, and_4_out, and_5_out, and_6_out, and_7_out, and_8_out, and_9_out,
       and_10_out, and_11_out, and_12_out, and_13_out, and_14_out, and_15_out, and_16_out, and_17_out,
       and_18_out, and_19_out, and_20_out, and_21_out, not_1_out, not_2_out, not_3_out, not_4_out, not_5_out,
       not_6_out, not_7_out, not_8_out, not_9_out, or_1_out, or_2_out;

  not not_1 (not_1_out, X);
  not not_2 (not_2_out, Y);
  not not_3 (not_3_out, X2);
  not not_4 (not_4_out, Y2);
  not not_5 (not_5_out, X3);
  not not_6 (not_6_out, Y3);
  not not_7 (not_7_out, Cin);
  not not_8 (not_8_out, or_1_out);
  not not_9 (not_9_out, or_2_out);
  and and_1 (and_1_out, X, not_2_out, not_7_out);
  and and_2 (and_2_out, not_1_out, Y, not_7_out);
  and and_3 (and_3_out, not_1_out, not_2_out, Cin);
  and and_4 (and_4_out, X, Y, Cin);
  and and_5 (and_5_out, Cin, X);
  and and_6 (and_6_out, Cin, Y);
  and and_7 (and_7_out, X, Y);
  and and_8 (and_8_out, X2, not_4_out, not_8_out);
  and and_9 (and_9_out, not_3_out, Y2, not_8_out);
  and and_10 (and_10_out, not_3_out, not_4_out, or_1_out);
  and and_11 (and_11_out, X2, Y2, or_1_out);
  and and_12 (and_12_out, or_1_out, X2);
  and and_13 (and_13_out, or_1_out, Y2);
  and and_14 (and_14_out, X2, Y2);
  and and_15 (and_15_out, X3, not_6_out, not_9_out);
  and and_16 (and_16_out, not_5_out, Y3, not_9_out);
  and and_17 (and_17_out, not_5_out, not_6_out, or_2_out);
  and and_18 (and_18_out, X3, Y3, or_2_out);
  and and_19 (and_19_out, or_2_out, X3);
  and and_20 (and_20_out, or_2_out, Y3);
  and and_21 (and_21_out, X3, Y3);
  or or_1 (or_1_out, and_5_out, and_6_out, and_7_out);
  or or_2 (or_2_out, and_12_out, and_13_out, and_14_out);
  or or_3 (Sum3, and_15_out, and_16_out, and_17_out, and_18_out);
  or or_4 (Cout, and_19_out, and_20_out, and_21_out);
  or or_5 (Sum1, and_1_out, and_2_out, and_3_out, and_4_out);
  or or_6 (Sum2, and_8_out, and_9_out, and_10_out, and_11_out);
  LED led_1 (.in(Sum1));
  LED led_2 (.in(Sum2));
  LED led_3 (.in(Sum3));
  LED led_4 (.in(Cout));

  // Notes on the sheet:
  //   First Cin should always be 0
endmodule
