// Logisim project BCD To 7-Seg.circ as structural Verilog: 1 circuit, main circuit main
module main (
  input  [3:0] in_1,
  input  [3:0] in_2,
  input  [3:0] in_3,
  input  in_4,
  input  in_5,
  input  in_6,
  input  [3:0] in_7,
  input  [3:0] in_8,
  input  [3:0] in_9,
  input  in_10,
  input  in_11,
  input  in_12,
  input  [3:0] in_13,
  input  [3:0] in_14,
  input  [3:0] in_15,
  input  in_16,
  input  in_17,
  input  in_18,
  input  [3:0] in_19,
  input  in_20
);

  wire decoder_1_out0, decoder_1_out1, decoder_1_out2, decoder_1_out3, decoder_1_out4, decoder_1_out5,
       decoder_1_out6, decoder_1_out7, decoder_1_out8, decoder_2_out0, decoder_2_out1, decoder_2_out2,
       decoder_2_out3, decoder_2_out4, decoder_2_out5, decoder_2_out6, decoder_2_out7, decoder_2_out8,
       decoder_3_out0, decoder_3_out1, decoder_3_out2, decoder_3_out3, decoder_3_out4, decoder_3_out5,
       decoder_3_out6, decoder_3_out7, decoder_3_out8, decoder_4_out0, decoder_4_out1, decoder_4_out2,
       decoder_4_out3, decoder_4_out4, decoder_4_out5, decoder_4_out6, decoder_4_out7, decoder_4_out8,
       decoder_5_out0, decoder_5_out1, decoder_5_out2, decoder_5_out3, decoder_5_out4, decoder_5_out5,
       decoder_5_out6, decoder_5_out7, decoder_5_out8, decoder_6_out0, decoder_6_out1, decoder_6_out2,
       decoder_6_out3, decoder_6_out4, decoder_6_out5, decoder_6_out6, decoder_6_out7, decoder_6_out8,
       decoder_7_out0, decoder_7_out1, decoder_7_out2, decoder_7_out3, decoder_7_out4, decoder_7_out5,
       decoder_7_out6, decoder_7_out7, decoder_7_out8, decoder_8_out0, decoder_8_out1, decoder_8_out2,
       decoder_8_out3, decoder_8_out4, decoder_8_out5, decoder_8_out6, decoder_8_out7, decoder_8_out8,
       decoder_9_out0, decoder_9_out1, decoder_9_out2, decoder_9_out3, decoder_9_out4, decoder_9_out5,
       decoder_9_out6, decoder_9_out7, decoder_9_out8, decoder_10_out0, decoder_10_out1, decoder_10_out2,
       decoder_10_out3, decoder_10_out4, decoder_10_out5, decoder_10_out6, decoder_10_out7, decoder_10_out8;
  wire [3:0] TR_2_out, TR_3_out, TR_4_out, TR_5_out, TR_6_out, TR_7_out, TR_8_out, TR_9_out, TR_10_out,
       TR_out, undriven, undriven_2, undriven_3, undriven_4, undriven_5, undriven_6, undriven_7, undriven_8,
       undriven_9, undriven_10;

  Decoder #(.select(4)) decoder_1 (
    .out0(decoder_1_out0), .out1(decoder_1_out1), .out2(decoder_1_out2), .out3(decoder_1_out3),
    .out4(decoder_1_out4), .out5(decoder_1_out5), .out6(decoder_1_out6), .out7(decoder_1_out7),
    .out8(decoder_1_out8), .sel(in_1), .en(in_4));  // open: out9, out10, out11, out12, out13, out14, out15
  Decoder #(.select(4)) decoder_2 (
    .out0(decoder_2_out0), .out1(decoder_2_out1), .out2(decoder_2_out2), .out3(decoder_2_out3),
    .out4(decoder_2_out4), .out5(decoder_2_out5), .out6(decoder_2_out6), .out7(decoder_2_out7),
    .out8(decoder_2_out8), .sel(in_7), .en(in_10));  // open: out9, out10, out11, out12, out13, out14, out15
  Decoder #(.select(4)) decoder_3 (
    .out0(decoder_3_out0), .out1(decoder_3_out1), .out2(decoder_3_out2), .out3(decoder_3_out3),
    .out4(decoder_3_out4), .out5(decoder_3_out5), .out6(decoder_3_out6), .out7(decoder_3_out7),
    .out8(decoder_3_out8), .sel(in_13), .en(in_16));  // open: out9, out10, out11, out12, out13, out14, out15
  Decoder #(.select(4)) decoder_4 (
    .out0(decoder_4_out0), .out1(decoder_4_out1), .out2(decoder_4_out2), .out3(decoder_4_out3),
    .out4(decoder_4_out4), .out5(decoder_4_out5), .out6(decoder_4_out6), .out7(decoder_4_out7),
    .out8(decoder_4_out8), .sel(in_19), .en(in_20));  // open: out9, out10, out11, out12, out13, out14, out15
  nor nor_1 (TR_out[1], decoder_1_out1, decoder_1_out4);
  nor TR (TR_out[0], decoder_1_out5, decoder_1_out6);
  not not_1 (undriven_2[1], decoder_1_out2);
  nor B (undriven_2[2], decoder_1_out1, decoder_1_out4, decoder_1_out7);
  nor nor_2 (TR_2_out[1], decoder_2_out1, decoder_2_out4);
  nor TR_2 (TR_2_out[0], decoder_2_out5, decoder_2_out6);
  not not_2 (undriven_3[1], decoder_2_out2);
  nor B_2 (undriven_3[2], decoder_2_out1, decoder_2_out4, decoder_2_out7);
  nor nor_3 (TR_3_out[1], decoder_3_out1, decoder_3_out4);
  nor TR_3 (TR_3_out[0], decoder_3_out5, decoder_3_out6);
  not not_3 (undriven_4[1], decoder_3_out2);
  nor B_3 (undriven_4[2], decoder_3_out1, decoder_3_out4, decoder_3_out7);
  nor nor_4 (TR_4_out[1], decoder_4_out1, decoder_4_out4);
  nor TR_4 (TR_4_out[0], decoder_4_out5, decoder_4_out6);
  not not_4 (undriven[1], decoder_4_out2);
  nor B_4 (undriven[2], decoder_4_out1, decoder_4_out4, decoder_4_out7);
  or BL (undriven_2[3], decoder_1_out0, decoder_1_out2, decoder_1_out6, decoder_1_out8);
  or BL_2 (undriven_3[3], decoder_2_out0, decoder_2_out2, decoder_2_out6, decoder_2_out8);
  or BL_3 (undriven_4[3], decoder_3_out0, decoder_3_out2, decoder_3_out6, decoder_3_out8);
  or BL_4 (undriven[3], decoder_4_out0, decoder_4_out2, decoder_4_out6, decoder_4_out8);
  nor TL (TR_out[2], decoder_1_out3, decoder_1_out2, decoder_1_out1, decoder_1_out7);
  nor M (TR_out[3], decoder_1_out0, decoder_1_out1, decoder_1_out7);
  nor TL_2 (TR_2_out[2], decoder_2_out3, decoder_2_out2, decoder_2_out1, decoder_2_out7);
  nor M_2 (TR_2_out[3], decoder_2_out0, decoder_2_out1, decoder_2_out7);
  nor TL_3 (TR_3_out[2], decoder_3_out3, decoder_3_out2, decoder_3_out1, decoder_3_out7);
  nor M_3 (TR_3_out[3], decoder_3_out0, decoder_3_out1, decoder_3_out7);
  nor TL_4 (TR_4_out[2], decoder_4_out3, decoder_4_out2, decoder_4_out1, decoder_4_out7);
  nor M_4 (TR_4_out[3], decoder_4_out0, decoder_4_out1, decoder_4_out7);
  _7_Segment_Display u_7_segment_display_1 (
    .g(TR_out[3]), .f(TR_out[2]), .a(TR_out[1]), .b(TR_out[0]), .e(undriven_2[3]), .d(undriven_2[2]),
    .c(undriven_2[1]), .dp(undriven_2[0]));
  Decoder #(.select(4)) decoder_5 (
    .out0(decoder_5_out0), .out1(decoder_5_out1), .out2(decoder_5_out2), .out3(decoder_5_out3),
    .out4(decoder_5_out4), .out5(decoder_5_out5), .out6(decoder_5_out6), .out7(decoder_5_out7),
    .out8(decoder_5_out8), .sel(in_2), .en(in_5));  // open: out9, out10, out11, out12, out13, out14, out15
  _7_Segment_Display u_7_segment_display_2 (
    .g(TR_2_out[3]), .f(TR_2_out[2]), .a(TR_2_out[1]), .b(TR_2_out[0]), .e(undriven_3[3]), .d(undriven_3[2]),
    .c(undriven_3[1]), .dp(undriven_3[0]));
  Decoder #(.select(4)) decoder_6 (
    .out0(decoder_6_out0), .out1(decoder_6_out1), .out2(decoder_6_out2), .out3(decoder_6_out3),
    .out4(decoder_6_out4), .out5(decoder_6_out5), .out6(decoder_6_out6), .out7(decoder_6_out7),
    .out8(decoder_6_out8), .sel(in_8), .en(in_11));  // open: out9, out10, out11, out12, out13, out14, out15
  _7_Segment_Display u_7_segment_display_3 (
    .g(TR_3_out[3]), .f(TR_3_out[2]), .a(TR_3_out[1]), .b(TR_3_out[0]), .e(undriven_4[3]), .d(undriven_4[2]),
    .c(undriven_4[1]), .dp(undriven_4[0]));
  Decoder #(.select(4)) decoder_7 (
    .out0(decoder_7_out0), .out1(decoder_7_out1), .out2(decoder_7_out2), .out3(decoder_7_out3),
    .out4(decoder_7_out4), .out5(decoder_7_out5), .out6(decoder_7_out6), .out7(decoder_7_out7),
    .out8(decoder_7_out8), .sel(in_14), .en(in_17));  // open: out9, out10, out11, out12, out13, out14, out15
  _7_Segment_Display u_7_segment_display_4 (
    .g(TR_4_out[3]), .f(TR_4_out[2]), .a(TR_4_out[1]), .b(TR_4_out[0]), .e(undriven[3]), .d(undriven[2]),
    .c(undriven[1]), .dp(undriven[0]));
  nor nor_5 (TR_5_out[1], decoder_5_out1, decoder_5_out4);
  nor TR_5 (TR_5_out[0], decoder_5_out5, decoder_5_out6);
  not not_5 (undriven_5[1], decoder_5_out2);
  nor B_5 (undriven_5[2], decoder_5_out1, decoder_5_out4, decoder_5_out7);
  nor nor_6 (TR_6_out[1], decoder_6_out1, decoder_6_out4);
  nor TR_6 (TR_6_out[0], decoder_6_out5, decoder_6_out6);
  not not_6 (undriven_6[1], decoder_6_out2);
  nor B_6 (undriven_6[2], decoder_6_out1, decoder_6_out4, decoder_6_out7);
  nor nor_7 (TR_7_out[1], decoder_7_out1, decoder_7_out4);
  nor TR_7 (TR_7_out[0], decoder_7_out5, decoder_7_out6);
  not not_7 (undriven_7[1], decoder_7_out2);
  nor B_7 (undriven_7[2], decoder_7_out1, decoder_7_out4, decoder_7_out7);
  or BL_5 (undriven_5[3], decoder_5_out0, decoder_5_out2, decoder_5_out6, decoder_5_out8);
  nor TL_5 (TR_5_out[2], decoder_5_out3, decoder_5_out2, decoder_5_out1, decoder_5_out7);
  nor M_5 (TR_5_out[3], decoder_5_out0, decoder_5_out1, decoder_5_out7);
  or BL_6 (undriven_6[3], decoder_6_out0, decoder_6_out2, decoder_6_out6, decoder_6_out8);
  nor TL_6 (TR_6_out[2], decoder_6_out3, decoder_6_out2, decoder_6_out1, decoder_6_out7);
  nor M_6 (TR_6_out[3], decoder_6_out0, decoder_6_out1, decoder_6_out7);
  or BL_7 (undriven_7[3], decoder_7_out0, decoder_7_out2, decoder_7_out6, decoder_7_out8);
  nor TL_7 (TR_7_out[2], decoder_7_out3, decoder_7_out2, decoder_7_out1, decoder_7_out7);
  nor M_7 (TR_7_out[3], decoder_7_out0, decoder_7_out1, decoder_7_out7);
  _7_Segment_Display u_7_segment_display_5 (
    .g(TR_5_out[3]), .f(TR_5_out[2]), .a(TR_5_out[1]), .b(TR_5_out[0]), .e(undriven_5[3]), .d(undriven_5[2]),
    .c(undriven_5[1]), .dp(undriven_5[0]));
  _7_Segment_Display u_7_segment_display_6 (
    .g(TR_6_out[3]), .f(TR_6_out[2]), .a(TR_6_out[1]), .b(TR_6_out[0]), .e(undriven_6[3]), .d(undriven_6[2]),
    .c(undriven_6[1]), .dp(undriven_6[0]));
  _7_Segment_Display u_7_segment_display_7 (
    .g(TR_7_out[3]), .f(TR_7_out[2]), .a(TR_7_out[1]), .b(TR_7_out[0]), .e(undriven_7[3]), .d(undriven_7[2]),
    .c(undriven_7[1]), .dp(undriven_7[0]));
  Decoder #(.select(4)) decoder_8 (
    .out0(decoder_8_out0), .out1(decoder_8_out1), .out2(decoder_8_out2), .out3(decoder_8_out3),
    .out4(decoder_8_out4), .out5(decoder_8_out5), .out6(decoder_8_out6), .out7(decoder_8_out7),
    .out8(decoder_8_out8), .sel(in_3), .en(in_6));  // open: out9, out10, out11, out12, out13, out14, out15
  Decoder #(.select(4)) decoder_9 (
    .out0(decoder_9_out0), .out1(decoder_9_out1), .out2(decoder_9_out2), .out3(decoder_9_out3),
    .out4(decoder_9_out4), .out5(decoder_9_out5), .out6(decoder_9_out6), .out7(decoder_9_out7),
    .out8(decoder_9_out8), .sel(in_9), .en(in_12));  // open: out9, out10, out11, out12, out13, out14, out15
  Decoder #(.select(4)) decoder_10 (
    .out0(decoder_10_out0), .out1(decoder_10_out1), .out2(decoder_10_out2), .out3(decoder_10_out3),
    .out4(decoder_10_out4), .out5(decoder_10_out5), .out6(decoder_10_out6), .out7(decoder_10_out7),
    .out8(decoder_10_out8), .sel(in_15), .en(in_18));  // open: out9, out10, out11, out12, out13, out14, out15
  nor nor_8 (TR_8_out[1], decoder_8_out1, decoder_8_out4);
  nor TR_8 (TR_8_out[0], decoder_8_out5, decoder_8_out6);
  not not_8 (undriven_8[1], decoder_8_out2);
  nor B_8 (undriven_8[2], decoder_8_out1, decoder_8_out4, decoder_8_out7);
  nor nor_9 (TR_9_out[1], decoder_9_out1, decoder_9_out4);
  nor TR_9 (TR_9_out[0], decoder_9_out5, decoder_9_out6);
  not not_9 (undriven_9[1], decoder_9_out2);
  nor B_9 (undriven_9[2], decoder_9_out1, decoder_9_out4, decoder_9_out7);
  nor nor_10 (TR_10_out[1], decoder_10_out1, decoder_10_out4);
  nor TR_10 (TR_10_out[0], decoder_10_out5, decoder_10_out6);
  not not_10 (undriven_10[1], decoder_10_out2);
  nor B_10 (undriven_10[2], decoder_10_out1, decoder_10_out4, decoder_10_out7);
  or BL_8 (undriven_8[3], decoder_8_out0, decoder_8_out2, decoder_8_out6, decoder_8_out8);
  or BL_9 (undriven_9[3], decoder_9_out0, decoder_9_out2, decoder_9_out6, decoder_9_out8);
  or BL_10 (undriven_10[3], decoder_10_out0, decoder_10_out2, decoder_10_out6, decoder_10_out8);
  nor TL_8 (TR_8_out[2], decoder_8_out3, decoder_8_out2, decoder_8_out1, decoder_8_out7);
  nor M_8 (TR_8_out[3], decoder_8_out0, decoder_8_out1, decoder_8_out7);
  nor TL_9 (TR_9_out[2], decoder_9_out3, decoder_9_out2, decoder_9_out1, decoder_9_out7);
  nor M_9 (TR_9_out[3], decoder_9_out0, decoder_9_out1, decoder_9_out7);
  nor TL_10 (TR_10_out[2], decoder_10_out3, decoder_10_out2, decoder_10_out1, decoder_10_out7);
  nor M_10 (TR_10_out[3], decoder_10_out0, decoder_10_out1, decoder_10_out7);
  _7_Segment_Display u_7_segment_display_8 (
    .g(TR_8_out[3]), .f(TR_8_out[2]), .a(TR_8_out[1]), .b(TR_8_out[0]), .e(undriven_8[3]), .d(undriven_8[2]),
    .c(undriven_8[1]), .dp(undriven_8[0]));
  _7_Segment_Display u_7_segment_display_9 (
    .g(TR_9_out[3]), .f(TR_9_out[2]), .a(TR_9_out[1]), .b(TR_9_out[0]), .e(undriven_9[3]), .d(undriven_9[2]),
    .c(undriven_9[1]), .dp(undriven_9[0]));
  _7_Segment_Display u_7_segment_display_10 (
    .g(TR_10_out[3]), .f(TR_10_out[2]), .a(TR_10_out[1]), .b(TR_10_out[0]), .e(undriven_10[3]),
    .d(undriven_10[2]), .c(undriven_10[1]), .dp(undriven_10[0]));

  // Notes on the sheet:
  //   T
  //   BR
  //   T
  //   BR
  //   T
  //   BR
  //   T
  //   BR
  //   TR
  //   T
  //   TL
  //   M
  //   TR
  //   T
  //   TL
  //   M
  //   TR
  //   T
  //   TL
  //   M
  //   TR
  //   T
  //   TL
  //   M
  //   M TL T TR
  //   M TL T TR
  //   M TL T TR
  //   M TL T TR
  //   T
  //   BR
  //   T
  //   BR
  //   T
  //   BR
  //   TR
  //   T
  //   TL
  //   M
  //   TR
  //   T
  //   TL
  //   M
  //   TR
  //   T
  //   TL
  //   M
  //   M TL T TR
  //   M TL T TR
  //   M TL T TR
  //   T
  //   BR
  //   T
  //   BR
  //   T
  //   BR
  //   TR
  //   T
  //   TL
  //   M
  //   TR
  //   T
  //   TL
  //   M
  //   TR
  //   T
  //   TL
  //   M
  //   M TL T TR
  //   M TL T TR
  //   M TL T TR
endmodule
