// Logisim project Modulo-10 Counter.circ as structural Verilog: 1 circuit, main circuit main
module main (
  input  in_1
);

  wire and_1_out, and_2_out, and_3_out, and_4_out, and_5_out, clock_1_out, j_k_ff_1_q, j_k_ff_2_q,
       j_k_ff_3_q, j_k_ff_4_q;

  and and_1 (and_1_out, in_1, j_k_ff_1_q);
  and and_2 (and_2_out, and_1_out, j_k_ff_2_q);
  and and_3 (and_3_out, and_2_out, j_k_ff_3_q);
  Clock clock_1 (.out(clock_1_out));
  J_K_Flip_Flop j_k_ff_1 (
    .J(in_1), .clk(clock_1_out), .K(in_1), .Q(j_k_ff_1_q), .reset(and_5_out));  // open: Qn, preset, en
  J_K_Flip_Flop j_k_ff_2 (
    .J(and_1_out), .clk(clock_1_out), .K(and_1_out), .Q(j_k_ff_2_q), .reset(and_5_out));  // open: Qn, preset, en
  J_K_Flip_Flop j_k_ff_3 (
    .J(and_2_out), .clk(clock_1_out), .K(and_2_out), .Q(j_k_ff_3_q), .reset(and_5_out));  // open: Qn, preset, en
  J_K_Flip_Flop j_k_ff_4 (
    .J(and_3_out), .clk(clock_1_out), .K(and_3_out), .Q(j_k_ff_4_q), .reset(and_5_out));  // open: Qn, preset, en
  and and_4 (and_4_out, j_k_ff_4_q, and_3_out);
  and and_5 (and_5_out, j_k_ff_2_q, j_k_ff_4_q);
endmodule
