// Logisim project Project 7base.circ as structural Verilog: 1 circuit, main circuit main
module main (
  input  in_1,
  input  in_2,
  input  in_3,
  input  [7:0] Input_1__8,
  input  [7:0] in_5,
  input  [2:0] Shift_bits__3,
  input  [2:0] in_7
);

  wire and_1_out, and_2_out, and_3_out, Clock_out, decoder_1_out8, decoder_1_out9, decoder_1_out10,
       decoder_1_out11, not_1_out, not_2_out, not_3_out, not_4_out, or_1_out, Reset_out, undriven_4;
  wire [1:0] counter_1_q;
  wire [3:0] adder_1_out, bitselector_2_out, PC_q, undriven, undriven_2;
  wire [7:0] adder_2_out, bitselector_3_out, decoder_1_out7, divider_1_out, Instruction_q, multiplier_1_out,
       negator_1_out, ram_1_data, shifter_1_out, shifter_2_out, subtractor_1_out, undriven_3;

  Button Clock (.out(Clock_out));
  Button Reset (.out(Reset_out));
  Counter #(.width(2), .max('h2)) counter_1 (
    .Q(counter_1_q), .clk(Clock_out), .clr(Reset_out));  // open: load, D, count, carry
  and and_1 (and_1_out, counter_1_q[1], not_1_out);
  not not_1 (not_1_out, counter_1_q[0]);
  not not_2 (not_2_out, counter_1_q[1]);
  and and_2 (and_2_out, not_2_out, counter_1_q[0]);
  Decoder #(.select(4), .disabled(0)) decoder_1 (
    .out0(decoder_1_out7[7]), .out1(decoder_1_out7[6]), .out2(decoder_1_out7[5]), .out3(decoder_1_out7[4]),
    .out4(decoder_1_out7[3]), .out5(decoder_1_out7[2]), .out6(decoder_1_out7[1]), .out7(decoder_1_out7[0]),
    .out8(decoder_1_out8), .out9(decoder_1_out9), .out10(decoder_1_out10), .out11(decoder_1_out11),
    .sel(undriven), .en(and_2_out));  // open: out12, out13, out14, out15
  not not_3 (not_3_out, in_3);
  Register Instruction (.D(bitselector_3_out), .en(and_3_out), .Q(Instruction_q), .clk(Clock_out), .clr(Reset_out));
  and and_3 (and_3_out, not_1_out, not_2_out);
  BitSelector #(.group(8)) bitselector_1 ();  // open: in, out, sel
  Register #(.width(4)) PC (.D(adder_1_out), .en(and_1_out), .Q(PC_q), .clk(Clock_out), .clr(Reset_out));
  Adder #(.width(4)) adder_1 (.a(4'b0000), .b(PC_q), .out(adder_1_out), .cin(not_3_out));  // open: cout
  not not_4 (not_4_out, and_3_out);
  BitSelector #(.group(4)) bitselector_2 (.in({undriven_2, PC_q}), .out(bitselector_2_out), .sel(not_4_out));
  RAM #(.addrWidth(4), .bus("separate")) ram_1 (
    .addr(bitselector_2_out), .din(undriven_3), .data(ram_1_data), .str(in_2), .clk(Clock_out), .ld(or_1_out));  // open: sel, clr
  or or_1 (or_1_out, and_3_out, undriven_4);
  Adder adder_2 (.a(decoder_1_out7), .b(in_5), .out(adder_2_out));  // open: cin, cout
  Subtractor subtractor_1 (.a(decoder_1_out7), .b(in_5), .out(subtractor_1_out));  // open: bin, bout
  Multiplier multiplier_1 (.a(decoder_1_out7), .b(in_5), .out(multiplier_1_out));  // open: cin, cout
  Divider divider_1 (.a(decoder_1_out7), .b(in_5), .out(divider_1_out));  // open: upper, rem
  Negator negator_1 (.in(decoder_1_out7), .out(negator_1_out));
  Shifter #(.shift("lr")) shifter_1 (.in(decoder_1_out7), .\dist (Shift_bits__3), .out(shifter_1_out));
  Shifter shifter_2 (.in(decoder_1_out7), .\dist (in_7), .out(shifter_2_out));
  BitSelector #(.width(16), .group(8)) bitselector_3 (
    .in({Instruction_q, ram_1_data}), .out(bitselector_3_out), .sel(in_1));

  // Notes on the sheet:
  //   Exit (1 disables PC increment)
  //   Remove the three 0 pins
  //   (They are for demo only)
  //   Execute Enable
  //   Decode Enable
  //   Note! 8 bits wide
  //   Note! 8 bits wide
  //   Instruction to be decoded
  //   Data from memory or temp register
  //   Note! 4 bits wide
  //   Address for memory operand
  //   Input 2 (8)
  //   Handy to have a reset on your accumulator and temp registers
  //   data from temp register
  //   Note! 8 bits wide
  //   True if loading to accumulator
  //   Note! 8 bits wide
  //   Load to Instruction register or accumulator
  //   select from memory or temp register
  //   True if storing from temp register
  //   Data from temp register
endmodule
