// Logisim project SR Flip-flop.circ as structural Verilog: 1 circuit, main circuit main
module main (
  input  S,
  input  R,
  input  in_3,
  input  in_4,
  output Q,
  output nQ,
  output out_7,
  output out_8
);

  wire clock_1_out, nand_1_out, nand_2_out;

  Clock clock_1 (.out(clock_1_out));
  nor nor_1 (Q, S, nQ);
  nor nor_2 (nQ, Q, R);
  nand nand_1 (nand_1_out, out_8, in_3, clock_1_out);
  nand nand_2 (nand_2_out, clock_1_out, out_7);
  nand nand_3 (out_7, nand_1_out, out_8);
  nand nand_4 (out_8, out_7, nand_2_out);
endmodule
