// Logisim project Study_Test1.circ as structural Verilog: 1 circuit, main circuit main
module main (
  input  in_1,
  input  Cin,
  input  in_3,
  input  x,
  input  y,
  input  in_6,
  input  in_7,
  input  in_8,
  input  in_9,
  input  Cin_2,
  input  x_2,
  input  y_2,
  output Cout,
  output out_14
);

  wire and_1_out, and_2_out, and_3_out, and_4_out, and_5_out, and_6_out, and_7_out, and_8_out, nand_1_out,
       nand_2_out, nand_3_out, not_1_out, not_2_out, not_3_out, not_4_out;

  not not_1 (not_1_out, y_2);
  not not_2 (not_2_out, Cin_2);
  not not_3 (not_3_out, Cin_2);
  and and_1 (and_1_out, Cin, x);
  and and_2 (and_2_out, x, y);
  and and_3 (and_3_out, Cin, y);
  and and_4 (and_4_out, not_2_out, not_1_out, Cin_2);
  and and_5 (and_5_out, not_2_out, not_3_out, y_2);
  and and_6 (and_6_out, not_1_out, not_3_out, Cin_2);
  and and_7 (and_7_out, Cin_2, y_2, Cin_2);
  or or_1 (Cout, and_1_out, and_2_out, and_3_out);
  or or_2 (out_14, and_4_out, and_5_out, and_6_out, and_7_out);
  not not_4 (not_4_out, in_3);
  not nand_1 (nand_1_out, in_1);  // NAND_Gate
  and and_8 (and_8_out, in_6, in_8);
  nand nand_2 (nand_2_out, in_7, in_9);
  nand nand_3 (nand_3_out, nand_2_out, nand_2_out);

  assign x_2 = Cin_2;

  // Notes on the sheet:
  //     Sum(X,Y,Cin) = (X!Y!Cin) + (!XY!Cin) + (!X!YCin) + (XYCin)
endmodule
